// Logisim project projeto_arcade.circ as structural Verilog: 20 circuits, main circuit main
module main (
  input  in_1,
  input  [3:0] in_2,
  input  [15:0] in_3
);

  wire clock_1_out, ctrl_display_1__0, ctrl_display_1__1, ctrl_display_1__2, ctrl_display_1__3,
       ctrl_display_1__4, ctrl_display_1__5, ctrl_display_1__6, ctrl_display_1__7, R_out, S_out;
  wire [15:0] memoria_16b_1_out;

  Clock clock_1 (.out(clock_1_out));
  Button R (.out(R_out));
  Button S (.out(S_out));
  Memoria_16b memoria_16b_1 (
    .S(S_out), .R(R_out), .Cl(clock_1_out), .W(in_1), .Data(in_3), .Andress(in_2), .Out(memoria_16b_1_out));
  Ctrl_Display ctrl_display_1 (
    .in_1(memoria_16b_1_out[3:0]), ._0(ctrl_display_1__0), ._1(ctrl_display_1__1), ._2(ctrl_display_1__2),
    ._3(ctrl_display_1__3), ._4(ctrl_display_1__4), ._5(ctrl_display_1__5), ._6(ctrl_display_1__6),
    ._7(ctrl_display_1__7));
  DotMatrix #(.inputtype("row"), .matrixcols(4), .matrixrows(4)) dotmatrix_1 (
    .row0(memoria_16b_1_out[3:0]), .row1(memoria_16b_1_out[7:4]), .row2(memoria_16b_1_out[11:8]),
    .row3(memoria_16b_1_out[15:12]));
  _7_Segment_Display u_7_segment_display_1 (
    .g(ctrl_display_1__3), .f(ctrl_display_1__2), .a(ctrl_display_1__1), .b(ctrl_display_1__0),
    .e(ctrl_display_1__7), .d(ctrl_display_1__6), .c(ctrl_display_1__5), .dp(ctrl_display_1__4));
endmodule

module FlipFlopD (
  input  R,
  input  D,
  input  CK,
  input  S,
  output Q
);

  wire and_1_out, and_2_out, nor_2_out, not_1_out;

  not not_1 (not_1_out, D);
  and and_1 (and_1_out, not_1_out, CK);
  and and_2 (and_2_out, CK, D);
  nor nor_1 (Q, R, and_1_out, nor_2_out);
  nor nor_2 (nor_2_out, Q, and_2_out, S);
endmodule

module Bit (
  input  R,
  input  D,
  input  CK,
  input  E,
  input  S,
  output Q
);

  wire and_1_out, flipflopd_1_q, not_1_out;

  and and_1 (and_1_out, CK, E);
  not not_1 (not_1_out, and_1_out);
  FlipFlopD flipflopd_1 (.D(D), .CK(not_1_out), .Q(flipflopd_1_q), .R(R), .S(S));
  FlipFlopD flipflopd_2 (.D(flipflopd_1_q), .CK(and_1_out), .Q(Q), .R(R), .S(S));
endmodule

module Palavra_8b (
  input  [7:0] Data,
  input  CK,
  input  E,
  input  R,
  input  S,
  output [7:0] Out
);

  Bit bit_1 (.D(Data[0]), .CK(CK), .E(E), .Q(Out[0]), .R(R), .S(S));
  Bit bit_2 (.D(Data[1]), .CK(CK), .E(E), .Q(Out[1]), .R(R), .S(S));
  Bit bit_3 (.D(Data[2]), .CK(CK), .E(E), .Q(Out[2]), .R(R), .S(S));
  Bit bit_4 (.D(Data[3]), .CK(CK), .E(E), .Q(Out[3]), .R(R), .S(S));
  Bit bit_5 (.D(Data[4]), .CK(CK), .E(E), .Q(Out[4]), .R(R), .S(S));
  Bit bit_6 (.D(Data[5]), .CK(CK), .E(E), .Q(Out[5]), .R(R), .S(S));
  Bit bit_7 (.D(Data[6]), .CK(CK), .E(E), .Q(Out[6]), .R(R), .S(S));
  Bit bit_8 (.D(Data[7]), .CK(CK), .E(E), .Q(Out[7]), .R(R), .S(S));
endmodule

module Memoria_8b (
  input  [2:0] Andress,
  input  [7:0] Data,
  input  Cl,
  input  W,
  input  S,
  input  R,
  output [7:0] Out
);

  wire and_1_out, multi_a_men_8b_1__0, multi_a_men_8b_1__1, multi_a_men_8b_1__2, multi_a_men_8b_1__3,
       multi_a_men_8b_1__4, multi_a_men_8b_1__5, multi_a_men_8b_1__6, multi_a_men_8b_1__7;
  wire [7:0] _0_out, _1_out, _2_out, _3_out, _4_out, _5_out, _6_out, _7_out;

  Multi_A_Men_8b multi_a_men_8b_1 (
    .in_1(Andress), ._0(multi_a_men_8b_1__0), ._1(multi_a_men_8b_1__1), ._2(multi_a_men_8b_1__2),
    ._3(multi_a_men_8b_1__3), ._4(multi_a_men_8b_1__4), ._5(multi_a_men_8b_1__5), ._6(multi_a_men_8b_1__6),
    ._7(multi_a_men_8b_1__7));
  and and_1 (and_1_out, Cl, W);
  Palavra_8b _7 (.Data(Data), .Out(_7_out), .CK(and_1_out), .E(multi_a_men_8b_1__7), .R(R), .S(S));
  Palavra_8b _6 (.Data(Data), .Out(_6_out), .CK(and_1_out), .E(multi_a_men_8b_1__6), .R(R), .S(S));
  Palavra_8b _5 (.Data(Data), .Out(_5_out), .CK(and_1_out), .E(multi_a_men_8b_1__5), .R(R), .S(S));
  Palavra_8b _4 (.Data(Data), .Out(_4_out), .CK(and_1_out), .E(multi_a_men_8b_1__4), .R(R), .S(S));
  Palavra_8b _3 (.Data(Data), .Out(_3_out), .CK(and_1_out), .E(multi_a_men_8b_1__3), .R(R), .S(S));
  Palavra_8b _2 (.Data(Data), .Out(_2_out), .CK(and_1_out), .E(multi_a_men_8b_1__2), .R(R), .S(S));
  Palavra_8b _1 (.Data(Data), .Out(_1_out), .CK(and_1_out), .E(multi_a_men_8b_1__1), .R(R), .S(S));
  Palavra_8b _0 (.Data(Data), .Out(_0_out), .CK(and_1_out), .E(multi_a_men_8b_1__0), .R(R), .S(S));
  Multi_B_Men_8b multi_b_men_8b_1 (
    ._7(_7_out), ._6(_6_out), ._5(_5_out), ._4(_4_out), ._3(_3_out), ._2(_2_out), ._1(_1_out), ._0(_0_out),
    .in_1(Andress), .out_10(Out));
endmodule

module Multi_A_Men_8b (
  input  [2:0] in_1,
  output _0,
  output _1,
  output _2,
  output _3,
  output _4,
  output _5,
  output _6,
  output _7
);

  and and_1 (_0, ~in_1[2], ~in_1[1], ~in_1[0]);  // AND_Gate
  and and_2 (_1, ~in_1[2], ~in_1[1], in_1[0]);  // AND_Gate
  and and_3 (_2, ~in_1[2], in_1[1], ~in_1[0]);  // AND_Gate
  and and_4 (_3, ~in_1[2], in_1[1], in_1[0]);  // AND_Gate
  and and_5 (_4, in_1[2], ~in_1[1], ~in_1[0]);  // AND_Gate
  and and_6 (_5, in_1[2], ~in_1[1], in_1[0]);  // AND_Gate
  and and_7 (_6, in_1[2], in_1[1], ~in_1[0]);  // AND_Gate
  and and_8 (_7, in_1[2], in_1[1], in_1[0]);
endmodule

module Multi_B_Men_8b (
  input  [2:0] in_1,
  input  [7:0] _7,
  input  [7:0] _6,
  input  [7:0] _5,
  input  [7:0] _4,
  input  [7:0] _3,
  input  [7:0] _2,
  input  [7:0] _1,
  input  [7:0] _0,
  output [7:0] out_10
);

  wire multi_a_men_8b_1__0, multi_a_men_8b_1__1, multi_a_men_8b_1__2, multi_a_men_8b_1__3,
       multi_a_men_8b_1__4, multi_a_men_8b_1__5, multi_a_men_8b_1__6, multi_a_men_8b_1__7;
  wire [7:0] select_8b_1_out, select_8b_2_out, select_8b_3_out, select_8b_4_out, select_8b_5_out,
       select_8b_6_out, select_8b_7_out, select_8b_8_out;

  Multi_A_Men_8b multi_a_men_8b_1 (
    .in_1(in_1), ._0(multi_a_men_8b_1__0), ._1(multi_a_men_8b_1__1), ._2(multi_a_men_8b_1__2),
    ._3(multi_a_men_8b_1__3), ._4(multi_a_men_8b_1__4), ._5(multi_a_men_8b_1__5), ._6(multi_a_men_8b_1__6),
    ._7(multi_a_men_8b_1__7));
  Select_8b select_8b_1 (.E(multi_a_men_8b_1__7), .In(_7), .Out(select_8b_1_out));
  Select_8b select_8b_2 (.E(multi_a_men_8b_1__6), .In(_6), .Out(select_8b_2_out));
  Select_8b select_8b_3 (.E(multi_a_men_8b_1__5), .In(_5), .Out(select_8b_3_out));
  Select_8b select_8b_4 (.E(multi_a_men_8b_1__4), .In(_4), .Out(select_8b_4_out));
  Select_8b select_8b_5 (.E(multi_a_men_8b_1__3), .In(_3), .Out(select_8b_5_out));
  Select_8b select_8b_6 (.E(multi_a_men_8b_1__2), .In(_2), .Out(select_8b_6_out));
  Select_8b select_8b_7 (.E(multi_a_men_8b_1__1), .In(_1), .Out(select_8b_7_out));
  Select_8b select_8b_8 (.E(multi_a_men_8b_1__0), .In(_0), .Out(select_8b_8_out));
  OR_Men_8b or_men_8b_1 (
    .out_9(out_10), .in_1(select_8b_8_out), .in_2(select_8b_7_out), .in_3(select_8b_6_out),
    .in_4(select_8b_5_out), .in_5(select_8b_4_out), .in_6(select_8b_3_out), .in_7(select_8b_2_out),
    .in_8(select_8b_1_out));
endmodule

module Select_8b (
  input  E,
  input  [7:0] In,
  output [7:0] Out
);

  and and_1 (Out[0], E, In[0]);
  and and_2 (Out[1], E, In[1]);
  and and_3 (Out[2], E, In[2]);
  and and_4 (Out[3], E, In[3]);
  and and_5 (Out[4], In[4], E);
  and and_6 (Out[5], In[5], E);
  and and_7 (Out[6], In[6], E);
  and and_8 (Out[7], In[7], E);
endmodule

module OR_Men_8b (
  input  [7:0] in_1,
  input  [7:0] in_2,
  input  [7:0] in_3,
  input  [7:0] in_4,
  input  [7:0] in_5,
  input  [7:0] in_6,
  input  [7:0] in_7,
  input  [7:0] in_8,
  output [7:0] out_9
);

  or or_1 (out_9[0], in_1[0], in_2[0], in_3[0], in_4[0], in_5[0], in_6[0], in_7[0], in_8[0]);
  or or_2 (out_9[1], in_1[1], in_2[1], in_3[1], in_4[1], in_5[1], in_6[1], in_7[1], in_8[1]);
  or or_3 (out_9[2], in_1[2], in_2[2], in_3[2], in_4[2], in_5[2], in_6[2], in_7[2], in_8[2]);
  or or_4 (out_9[3], in_1[3], in_2[3], in_3[3], in_4[3], in_5[3], in_6[3], in_7[3], in_8[3]);
  or or_5 (out_9[4], in_1[4], in_2[4], in_3[4], in_4[4], in_5[4], in_6[4], in_7[4], in_8[4]);
  or or_6 (out_9[5], in_1[5], in_2[5], in_3[5], in_4[5], in_5[5], in_6[5], in_7[5], in_8[5]);
  or or_7 (out_9[6], in_1[6], in_2[6], in_3[6], in_4[6], in_5[6], in_6[6], in_7[6], in_8[6]);
  or or_8 (out_9[7], in_1[7], in_2[7], in_3[7], in_4[7], in_5[7], in_6[7], in_7[7], in_8[7]);
endmodule

module Ctrl_Display_Ate_9 (
  input  [3:0] in_1,
  output _0,
  output _1,
  output _2,
  output _3,
  output _4,
  output _5,
  output _6,
  output _7
);

  wire and_1_out, and_2_out, and_3_out, and_4_out, and_5_out, and_6_out, and_7_out, and_8_out, and_9_out,
       and_10_out, and_11_out, and_12_out, and_13_out, and_14_out, and_15_out, and_16_out;

  and and_1 (and_1_out, ~in_1[1], ~in_1[0]);  // AND_Gate
  and and_2 (and_2_out, in_1[0], in_1[1]);
  and and_3 (and_3_out, ~in_1[2], ~in_1[0]);  // AND_Gate
  and and_4 (and_4_out, in_1[2], in_1[0]);
  and and_5 (and_5_out, ~in_1[1], ~in_1[0]);  // AND_Gate
  and and_6 (and_6_out, in_1[2], ~in_1[1]);  // AND_Gate
  and and_7 (and_7_out, in_1[2], ~in_1[0]);  // AND_Gate
  and and_8 (and_8_out, ~in_1[2], in_1[1]);  // AND_Gate
  and and_9 (and_9_out, in_1[1], ~in_1[0]);  // AND_Gate
  and and_10 (and_10_out, in_1[2], ~in_1[1]);  // AND_Gate
  and and_11 (and_11_out, ~in_1[2], ~in_1[0]);  // AND_Gate
  and and_12 (and_12_out, ~in_1[2], in_1[1]);  // AND_Gate
  and and_13 (and_13_out, in_1[1], ~in_1[0]);  // AND_Gate
  and and_14 (and_14_out, in_1[2], ~in_1[1], in_1[0]);  // AND_Gate
  and and_15 (and_15_out, ~in_1[2], ~in_1[0]);  // AND_Gate
  and and_16 (and_16_out, in_1[1], ~in_1[0]);  // AND_Gate
  or or_1 (_0, and_1_out, ~in_1[2], and_2_out);  // OR_Gate
  or or_2 (_1, in_1[3], in_1[1], and_3_out, and_4_out);
  or or_3 (_2, in_1[3], and_5_out, and_6_out, and_7_out);
  or or_4 (_3, in_1[3], and_8_out, and_9_out, and_10_out);
  or or_5 (_5, ~in_1[1], in_1[0], in_1[2]);  // OR_Gate
  or or_6 (_6, in_1[3], and_11_out, and_12_out, and_13_out, and_14_out);
  or or_7 (_7, and_15_out, and_16_out);
  Button button_1 (.out(_4));
endmodule

module Add (
  input  A,
  input  B,
  input  Of_in,
  output Of_out,
  output Out
);

  wire and_1_out, and_2_out, and_3_out, and_4_out, and_5_out, and_6_out, and_7_out;

  and and_1 (and_1_out, A, B);
  and and_2 (and_2_out, Of_in, B);
  and and_3 (and_3_out, Of_in, A);
  and and_4 (and_4_out, ~Of_in, ~A, B);  // AND_Gate
  and and_5 (and_5_out, ~Of_in, A, ~B);  // AND_Gate
  and and_6 (and_6_out, Of_in, ~A, ~B);  // AND_Gate
  and and_7 (and_7_out, Of_in, A, B);
  or or_1 (Of_out, and_1_out, and_2_out, and_3_out);
  or or_2 (Out, and_4_out, and_5_out, and_6_out, and_7_out);
endmodule

module Somador (
  input  [7:0] A,
  input  [7:0] B,
  output [7:0] Out
);

  wire add_1_of_out, add_2_of_out, add_3_of_out, add_4_of_out, add_5_of_out, add_6_of_out, add_7_of_out,
       add_8_of_out, button_1_out;

  Button button_1 (.out(button_1_out));
  Add add_1 (.B(B[0]), .A(A[0]), .Of_in(button_1_out), .Of_out(add_1_of_out), .Out(Out[0]));
  Add add_2 (.B(B[1]), .A(A[1]), .Of_in(add_1_of_out), .Of_out(add_2_of_out), .Out(Out[1]));
  Add add_3 (.B(B[2]), .A(A[2]), .Of_in(add_2_of_out), .Of_out(add_3_of_out), .Out(Out[2]));
  Add add_4 (.B(B[3]), .A(A[3]), .Of_in(add_3_of_out), .Of_out(add_4_of_out), .Out(Out[3]));
  Add add_5 (.B(B[4]), .A(A[4]), .Of_in(add_4_of_out), .Of_out(add_5_of_out), .Out(Out[4]));
  Add add_6 (.B(B[5]), .A(A[5]), .Of_in(add_5_of_out), .Of_out(add_6_of_out), .Out(Out[5]));
  Add add_7 (.B(B[6]), .A(A[6]), .Of_in(add_6_of_out), .Of_out(add_7_of_out), .Out(Out[6]));
  Add add_8 (.B(B[7]), .A(A[7]), .Of_in(add_7_of_out), .Of_out(add_8_of_out), .Out(Out[7]));
  LED led_1 (.in(add_8_of_out));
endmodule

module Ctrl_Display (
  input  [3:0] in_1,
  output _0,
  output _1,
  output _2,
  output _3,
  output _4,
  output _5,
  output _6,
  output _7
);

  wire and_1_out, and_2_out, and_3_out, and_4_out, and_5_out, and_6_out, and_7_out, and_8_out, and_9_out,
       and_10_out, and_11_out, and_12_out, and_13_out, and_14_out, and_15_out, and_16_out, and_17_out,
       and_18_out, and_19_out;

  and and_1 (and_1_out, ~in_1[0], ~in_1[1]);  // AND_Gate
  and and_2 (and_2_out, in_1[0], in_1[1]);
  and and_3 (and_3_out, in_1[0], in_1[2]);
  and and_4 (and_4_out, ~in_1[0], ~in_1[2]);  // AND_Gate
  and and_5 (and_5_out, ~in_1[1], ~in_1[0]);  // AND_Gate
  and and_6 (and_6_out, ~in_1[1], in_1[2]);  // AND_Gate
  and and_7 (and_7_out, in_1[2], ~in_1[0]);  // AND_Gate
  and and_8 (and_8_out, ~in_1[3], ~in_1[2], in_1[1]);  // AND_Gate
  and and_9 (and_9_out, ~in_1[3], ~in_1[0], in_1[1]);  // AND_Gate
  and and_10 (and_10_out, ~in_1[3], ~in_1[1], in_1[2]);  // AND_Gate
  and and_11 (and_11_out, ~in_1[1], ~in_1[2], in_1[3]);  // AND_Gate
  and and_12 (and_12_out, ~in_1[2], ~in_1[0]);  // AND_Gate
  and and_13 (and_13_out, in_1[1], ~in_1[2]);  // AND_Gate
  and and_14 (and_14_out, in_1[1], ~in_1[0]);  // AND_Gate
  and and_15 (and_15_out, in_1[2], ~in_1[1], in_1[0]);  // AND_Gate
  and and_16 (and_16_out, ~in_1[2], ~in_1[0]);  // AND_Gate
  and and_17 (and_17_out, in_1[1], ~in_1[0]);  // AND_Gate
  and and_18 (and_18_out, in_1[3], in_1[1]);
  and and_19 (and_19_out, in_1[3], in_1[2]);
  or or_1 (_0, ~in_1[2], in_1[3], and_1_out, and_2_out);  // OR_Gate
  or or_2 (_1, in_1[1], in_1[3], and_3_out, and_4_out);
  or or_3 (_2, in_1[3], and_5_out, and_6_out, and_7_out);
  or or_4 (_3, and_8_out, and_9_out, and_10_out, and_11_out);
  or or_5 (_5, ~in_1[1], in_1[0], in_1[2], in_1[3]);  // OR_Gate
  or or_6 (_6, in_1[3], and_12_out, and_13_out, and_14_out, and_15_out);
  or or_7 (_7, and_16_out, and_17_out, and_18_out, and_19_out);
  Button button_1 (.out(_4));
endmodule

module Memoria_16b (
  input  S,
  input  R,
  input  Cl,
  input  W,
  input  [15:0] Data,
  input  [3:0] Andress,
  output [15:0] Out
);

  wire and_1_out;
  wire [7:0] multi_a_men_16_1_out_2;
  wire [15:0] _0, _1, _2, _3, _4, _5, _6, _7, _8, _9, A, B, C, D, E, F;
  wire [15:8] multi_a_men_16_1_out_2_2;

  Multi_A_Men_16 multi_a_men_16_1 (.in_1(Andress), .out_2({multi_a_men_16_1_out_2_2, multi_a_men_16_1_out_2}));
  and and_1 (and_1_out, Cl, W);
  Palavra_16b palavra_16b_1 (.Data(Data), .Out(_0), .CK(and_1_out), .E(multi_a_men_16_1_out_2[0]), .R(R), .S(S));
  Palavra_16b palavra_16b_2 (.Data(Data), .Out(_8), .CK(and_1_out), .E(multi_a_men_16_1_out_2_2[8]), .R(R), .S(S));
  Multi_B_Men_16b multi_b_men_16b_1 (
    ._15(F), ._14(E), ._13(D), ._12(C), ._11(B), ._10(A), ._9(_9), ._8(_8), ._7(_7), ._6(_6), ._5(_5),
    ._4(_4), ._3(_3), ._2(_2), ._1(_1), ._0(_0), .Adress(Andress), .Out(Out));
  Palavra_16b palavra_16b_3 (.Data(Data), .Out(_1), .CK(and_1_out), .E(multi_a_men_16_1_out_2[1]), .R(R), .S(S));
  Palavra_16b palavra_16b_4 (.Data(Data), .Out(_9), .CK(and_1_out), .E(multi_a_men_16_1_out_2_2[9]), .R(R), .S(S));
  Palavra_16b palavra_16b_5 (.Data(Data), .Out(_2), .CK(and_1_out), .E(multi_a_men_16_1_out_2[2]), .R(R), .S(S));
  Palavra_16b palavra_16b_6 (.Data(Data), .Out(A), .CK(and_1_out), .E(multi_a_men_16_1_out_2_2[10]), .R(R), .S(S));
  Palavra_16b palavra_16b_7 (.Data(Data), .Out(_3), .CK(and_1_out), .E(multi_a_men_16_1_out_2[3]), .R(R), .S(S));
  Palavra_16b palavra_16b_8 (.Data(Data), .Out(B), .CK(and_1_out), .E(multi_a_men_16_1_out_2_2[11]), .R(R), .S(S));
  Palavra_16b palavra_16b_9 (.Data(Data), .Out(_4), .CK(and_1_out), .E(multi_a_men_16_1_out_2[4]), .R(R), .S(S));
  Palavra_16b palavra_16b_10 (.Data(Data), .Out(C), .CK(and_1_out), .E(multi_a_men_16_1_out_2_2[12]), .R(R), .S(S));
  Palavra_16b palavra_16b_11 (.Data(Data), .Out(_5), .CK(and_1_out), .E(multi_a_men_16_1_out_2[5]), .R(R), .S(S));
  Palavra_16b palavra_16b_12 (.Data(Data), .Out(D), .CK(and_1_out), .E(multi_a_men_16_1_out_2_2[13]), .R(R), .S(S));
  Palavra_16b palavra_16b_13 (.Data(Data), .Out(_6), .CK(and_1_out), .E(multi_a_men_16_1_out_2[6]), .R(R), .S(S));
  Palavra_16b palavra_16b_14 (.Data(Data), .Out(E), .CK(and_1_out), .E(multi_a_men_16_1_out_2_2[14]), .R(R), .S(S));
  Palavra_16b palavra_16b_15 (.Data(Data), .Out(_7), .CK(and_1_out), .E(multi_a_men_16_1_out_2[7]), .R(R), .S(S));
  Palavra_16b palavra_16b_16 (.Data(Data), .Out(F), .CK(and_1_out), .E(multi_a_men_16_1_out_2_2[15]), .R(R), .S(S));
endmodule

module Palavra_16b (
  input  CK,
  input  R,
  input  S,
  input  [15:0] Data,
  input  E,
  output [15:0] Out
);

  Palavra_8b palavra_8b_1 (.Data(Data[7:0]), .Out(Out[7:0]), .CK(CK), .E(E), .R(R), .S(S));
  Palavra_8b palavra_8b_2 (.Data(Data[15:8]), .Out(Out[15:8]), .CK(CK), .E(E), .R(R), .S(S));
endmodule

module Multi_A_Men_16 (
  input  [3:0] in_1,
  output [15:0] out_2
);

  and and_1 (out_2[0], ~in_1[3], ~in_1[2], ~in_1[1], ~in_1[0]);  // AND_Gate
  and and_2 (out_2[1], ~in_1[3], ~in_1[2], ~in_1[1], in_1[0]);  // AND_Gate
  and and_3 (out_2[2], ~in_1[3], ~in_1[2], in_1[1], ~in_1[0]);  // AND_Gate
  and and_4 (out_2[3], ~in_1[3], ~in_1[2], in_1[1], in_1[0]);  // AND_Gate
  and and_5 (out_2[4], ~in_1[3], in_1[2], ~in_1[1], ~in_1[0]);  // AND_Gate
  and and_6 (out_2[5], ~in_1[3], in_1[2], ~in_1[1], in_1[0]);  // AND_Gate
  and and_7 (out_2[6], ~in_1[3], in_1[2], in_1[1], ~in_1[0]);  // AND_Gate
  and and_8 (out_2[7], ~in_1[3], in_1[2], in_1[1], in_1[0]);  // AND_Gate
  and and_9 (out_2[8], in_1[3], ~in_1[2], ~in_1[1], ~in_1[0]);  // AND_Gate
  and and_10 (out_2[9], in_1[3], ~in_1[2], ~in_1[1], in_1[0]);  // AND_Gate
  and and_11 (out_2[10], in_1[3], ~in_1[2], in_1[1], ~in_1[0]);  // AND_Gate
  and and_12 (out_2[11], in_1[3], ~in_1[2], in_1[1], in_1[0]);  // AND_Gate
  and and_13 (out_2[12], in_1[3], in_1[2], ~in_1[1], ~in_1[0]);  // AND_Gate
  and and_14 (out_2[13], in_1[3], in_1[2], ~in_1[1], in_1[0]);  // AND_Gate
  and and_15 (out_2[14], in_1[3], in_1[2], in_1[1], ~in_1[0]);  // AND_Gate
  and and_16 (out_2[15], in_1[3], in_1[2], in_1[1], in_1[0]);
endmodule

module Select_16b (
  input  E,
  input  [15:0] In,
  output [15:0] Out
);

  and and_1 (Out[0], E, In[0]);
  and and_2 (Out[1], E, In[1]);
  and and_3 (Out[2], E, In[2]);
  and and_4 (Out[3], E, In[3]);
  and and_5 (Out[4], E, In[4]);
  and and_6 (Out[5], E, In[5]);
  and and_7 (Out[6], E, In[6]);
  and and_8 (Out[7], E, In[7]);
  and and_9 (Out[8], In[8], E);
  and and_10 (Out[9], In[9], E);
  and and_11 (Out[10], In[10], E);
  and and_12 (Out[11], In[11], E);
  and and_13 (Out[12], In[12], E);
  and and_14 (Out[13], In[13], E);
  and and_15 (Out[14], In[14], E);
  and and_16 (Out[15], In[15], E);
endmodule

module Multi_B_Men_16b (
  input  [3:0] Adress,
  input  [15:0] _15,
  input  [15:0] _14,
  input  [15:0] _13,
  input  [15:0] _12,
  input  [15:0] _11,
  input  [15:0] _10,
  input  [15:0] _9,
  input  [15:0] _8,
  input  [15:0] _7,
  input  [15:0] _6,
  input  [15:0] _5,
  input  [15:0] _4,
  input  [15:0] _3,
  input  [15:0] _2,
  input  [15:0] _1,
  input  [15:0] _0,
  output [15:0] Out
);

  wire [15:0] multi_a_men_16_1_out_2, select_16b_1_out, select_16b_2_out, select_16b_3_out, select_16b_4_out,
       select_16b_5_out, select_16b_6_out, select_16b_7_out, select_16b_8_out, select_16b_9_out,
       select_16b_10_out, select_16b_11_out, select_16b_12_out, select_16b_13_out, select_16b_14_out,
       select_16b_15_out, select_16b_16_out;

  Multi_A_Men_16 multi_a_men_16_1 (.in_1(Adress), .out_2(multi_a_men_16_1_out_2));
  Select_16b select_16b_1 (.In(_15), .Out(select_16b_1_out), .E(multi_a_men_16_1_out_2[15]));
  Select_16b select_16b_2 (.In(_14), .Out(select_16b_2_out), .E(multi_a_men_16_1_out_2[14]));
  Select_16b select_16b_3 (.In(_13), .Out(select_16b_3_out), .E(multi_a_men_16_1_out_2[13]));
  Select_16b select_16b_4 (.In(_12), .Out(select_16b_4_out), .E(multi_a_men_16_1_out_2[12]));
  Select_16b select_16b_5 (.In(_11), .Out(select_16b_5_out), .E(multi_a_men_16_1_out_2[11]));
  Select_16b select_16b_6 (.In(_10), .Out(select_16b_6_out), .E(multi_a_men_16_1_out_2[10]));
  Select_16b select_16b_7 (.In(_9), .Out(select_16b_7_out), .E(multi_a_men_16_1_out_2[9]));
  Select_16b select_16b_8 (.In(_8), .Out(select_16b_8_out), .E(multi_a_men_16_1_out_2[8]));
  Select_16b select_16b_9 (.In(_7), .Out(select_16b_9_out), .E(multi_a_men_16_1_out_2[7]));
  Select_16b select_16b_10 (.In(_6), .Out(select_16b_10_out), .E(multi_a_men_16_1_out_2[6]));
  Select_16b select_16b_11 (.In(_5), .Out(select_16b_11_out), .E(multi_a_men_16_1_out_2[5]));
  Select_16b select_16b_12 (.In(_4), .Out(select_16b_12_out), .E(multi_a_men_16_1_out_2[4]));
  Select_16b select_16b_13 (.In(_3), .Out(select_16b_13_out), .E(multi_a_men_16_1_out_2[3]));
  Select_16b select_16b_14 (.In(_2), .Out(select_16b_14_out), .E(multi_a_men_16_1_out_2[2]));
  Select_16b select_16b_15 (.In(_1), .Out(select_16b_15_out), .E(multi_a_men_16_1_out_2[1]));
  Select_16b select_16b_16 (.In(_0), .Out(select_16b_16_out), .E(multi_a_men_16_1_out_2[0]));
  OR_Men_16b or_men_16b_1 (
    ._15(select_16b_1_out), ._14(select_16b_2_out), ._13(select_16b_3_out), ._12(select_16b_4_out),
    ._11(select_16b_5_out), ._10(select_16b_6_out), ._9(select_16b_7_out), ._8(select_16b_8_out),
    ._7(select_16b_9_out), ._6(select_16b_10_out), ._5(select_16b_11_out), ._4(select_16b_12_out),
    ._3(select_16b_13_out), ._2(select_16b_14_out), ._1(select_16b_15_out), ._0(select_16b_16_out),
    .out_17(Out));
endmodule

module OR_Men_16b (
  input  [15:0] _15,
  input  [15:0] _14,
  input  [15:0] _13,
  input  [15:0] _12,
  input  [15:0] _11,
  input  [15:0] _10,
  input  [15:0] _9,
  input  [15:0] _8,
  input  [15:0] _7,
  input  [15:0] _6,
  input  [15:0] _5,
  input  [15:0] _4,
  input  [15:0] _3,
  input  [15:0] _2,
  input  [15:0] _1,
  input  [15:0] _0,
  output [15:0] out_17
);

  assign out_17 = _15 | _14 | _13 | _12 | _11 | _10 | _9 | _8 | _7 | _6 | _5 | _4 | _3 | _2 | _1 | _0;  // OR_Gate or_1, 16 bits wide
endmodule

module Contador (
  input  [7:0] in_1
);

  wire button_1_out, button_2_out, clock_1_out, ctrl_display_1__0, ctrl_display_1__1, ctrl_display_1__2,
       ctrl_display_1__3, ctrl_display_1__4, ctrl_display_1__5, ctrl_display_1__6, ctrl_display_1__7;
  wire [7:0] palavra_8b_1_out, somador_1_out;

  Clock clock_1 (.out(clock_1_out));
  RAM ram_1 ();  // open: addr, data, sel, clk, ld, clr
  Button button_1 (.out(button_1_out));
  Button button_2 (.out(button_2_out));
  Palavra_8b palavra_8b_1 (
    .Data(somador_1_out), .Out(palavra_8b_1_out), .CK(clock_1_out), .E(clock_1_out), .R(button_1_out),
    .S(button_2_out));
  Somador somador_1 (.A(palavra_8b_1_out), .B(in_1), .Out(somador_1_out));
  Ctrl_Display ctrl_display_1 (
    .in_1(somador_1_out[3:0]), ._0(ctrl_display_1__0), ._1(ctrl_display_1__1), ._2(ctrl_display_1__2),
    ._3(ctrl_display_1__3), ._4(ctrl_display_1__4), ._5(ctrl_display_1__5), ._6(ctrl_display_1__6),
    ._7(ctrl_display_1__7));
  _7_Segment_Display u_7_segment_display_1 (
    .g(ctrl_display_1__3), .f(ctrl_display_1__2), .a(ctrl_display_1__1), .b(ctrl_display_1__0),
    .e(ctrl_display_1__7), .d(ctrl_display_1__6), .c(ctrl_display_1__5), .dp(ctrl_display_1__4));
endmodule
